// Logisim project project3.circ as structural Verilog: 2 circuits, main circuit Control Unit
module Control_Unit (
);

  wire ADDRMODE, and_1_out, and_2_out, and_3_out, and_4_out, and_5_out, and_6_out, and_7_out, and_8_out,
       and_9_out, and_10_out, and_11_out, and_12_out, and_13_out, and_14_out, and_15_out, and_16_out,
       and_17_out, and_18_out, and_19_out, and_20_out, and_21_out, and_22_out, and_23_out, and_24_out,
       and_25_out, and_26_out, and_27_out, and_28_out, and_29_out, and_30_out, and_31_out, and_32_out,
       and_33_out, and_34_out, and_35_out, and_36_out, and_37_out, and_38_out, and_39_out, and_40_out,
       and_41_out, and_42_out, and_43_out, and_44_out, and_45_out, and_46_out, and_47_out, D00, D0A, D0B,
       D0C, D0D, D0E, D01, D02, D03, D04, D05, D06, D07, D08, D09, decoder_4_out6, decoder_4_out7,
       decoder_5_out6, decoder_5_out7, decoder_6_out6, decoder_6_out7, IR_Enable, IR_LH, Mem_clr, Mem_load,
       Mem_sel, Mem_str, not_1_out, not_2_out, not_3_out, not_4_out, not_5_out, not_6_out, not_7_out,
       not_8_out, not_9_out, not_10_out, not_11_out, not_12_out, SC_Reset, SR_Reset, T0, T1, T2, T3, T4, T5,
       T6, T7, xor_1_out, xor_2_out;
  wire [1:0] AR_FunSel, AR_OutCSel, AR_OutSel, IR_FunSel, MuxASel, MuxBSel, RF_FunSel, RF_OutASel,
       RF_OutBSel, RF_OutSel;
  wire [2:0] AR_RegSel, or_1_out, or_2_out, or_3_out;
  wire [2:1] DESTREG;
  wire [3:0] ALU_FunSel, decoder_4_out3, decoder_5_out3, RF_RegSel;
  wire [7:0] ADDRESS;
  wire [15:11] Instruction;

  Sequence_Counter sequence_counter_1 (
    .Reset(SC_Reset), .T0(T0), .T1(T1), .T2(T2), .T3(T3), .T4(T4), .T5(T5), .T6(T6), .T7(T7));
  and and_1 (and_1_out, D09, T3);
  Organization organization_1 (
    .OutASel(RF_OutASel), .FunSel(ALU_FunSel), .OutBSel(RF_OutBSel), .FunSel_2(RF_FunSel),
    .RegSel(RF_RegSel), .MuxASel(MuxASel), .MuxBSel(MuxBSel), .OutCSel(AR_OutCSel), .FunSel_3(AR_FunSel),
    .RegSel_2(AR_RegSel), .L_H(IR_LH), .Enable(IR_Enable), .FunSel_4(IR_FunSel), .in_7(Mem_str),
    .in_8(Mem_sel), .in_9(Mem_load), .in_10(Mem_clr), .Instruction({Instruction, DESTREG, ADDRMODE, ADDRESS}));
  not not_1 (not_1_out, ADDRMODE);
  and and_2 (and_2_out, D09, T2);
  and and_3 (and_3_out, and_2_out, not_1_out);
  assign AR_FunSel = and_3_out ? 2'b00 : 2'bz;  // Controlled_Buffer controlled_buffer_1
  assign AR_RegSel = and_3_out ? 3'b100 : 3'bz;  // Controlled_Buffer controlled_buffer_2
  assign MuxBSel = and_3_out ? 2'b01 : 2'bz;  // Controlled_Buffer controlled_buffer_3
  not not_2 (not_2_out, ADDRMODE);
  and and_4 (and_4_out, and_1_out, not_2_out);
  assign AR_OutSel = and_4_out ? 2'b00 : 2'bz;  // Controlled_Buffer controlled_buffer_4
  assign MuxASel = and_4_out ? 2'b01 : 2'bz;  // Controlled_Buffer controlled_buffer_5
  Decoder #(.select(2), .disabled(0)) decoder_1 (
    .out0(RF_RegSel[3]), .out1(RF_RegSel[2]), .out2(RF_RegSel[1]), .out3(RF_RegSel[0]), .sel(DESTREG),
    .en(and_4_out));
  not not_3 (not_3_out, ADDRMODE);
  and and_5 (and_5_out, D09, T3);
  and and_6 (and_6_out, and_5_out, not_3_out);
  assign SR_Reset = and_6_out ? 1'b1 : 1'bz;  // Controlled_Buffer controlled_buffer_6
  and and_7 (and_7_out, D09, T2);
  and and_8 (and_8_out, and_7_out, ADDRMODE);
  assign MuxASel = and_8_out ? 2'b00 : 2'bz;  // Controlled_Buffer controlled_buffer_7
  Decoder #(.select(2), .disabled(0)) decoder_2 (
    .out0(RF_RegSel[3]), .out1(RF_RegSel[2]), .out2(RF_RegSel[1]), .out3(RF_RegSel[0]), .sel(DESTREG),
    .en(and_8_out));
  and and_9 (and_9_out, D09, T2);
  and and_10 (and_10_out, and_9_out, ADDRMODE);
  assign SR_Reset = and_10_out ? 1'b1 : 1'bz;  // Controlled_Buffer controlled_buffer_8
  assign IR_LH = T0 ? 1'b0 : 1'bz;  // Controlled_Buffer controlled_buffer_9
  assign IR_Enable = T0 ? 1'b1 : 1'bz;  // Controlled_Buffer controlled_buffer_10
  assign IR_FunSel = T0 ? 2'b00 : 2'bz;  // Controlled_Buffer controlled_buffer_11
  assign Mem_load = T0 ? 1'b1 : 1'bz;  // Controlled_Buffer controlled_buffer_12
  assign Mem_str = T0 ? 1'b0 : 1'bz;  // Controlled_Buffer controlled_buffer_13
  assign Mem_sel = T0 ? 1'b0 : 1'bz;  // Controlled_Buffer controlled_buffer_14
  assign Mem_clr = T0 ? 1'b0 : 1'bz;  // Controlled_Buffer controlled_buffer_15
  assign AR_FunSel = T0 ? 2'b10 : 2'bz;  // Controlled_Buffer controlled_buffer_16
  assign AR_RegSel = T0 ? 3'b001 : 3'bz;  // Controlled_Buffer controlled_buffer_17
  assign AR_OutCSel = T0 ? 2'b10 : 2'bz;  // Controlled_Buffer controlled_buffer_18
  and and_11 (and_11_out, D0A, T2);
  and and_12 (and_12_out, D0A, T4);
  assign IR_LH = T1 ? 1'b1 : 1'bz;  // Controlled_Buffer controlled_buffer_19
  assign IR_Enable = T1 ? 1'b1 : 1'bz;  // Controlled_Buffer controlled_buffer_20
  assign IR_FunSel = T1 ? 2'b00 : 2'bz;  // Controlled_Buffer controlled_buffer_21
  assign Mem_load = T1 ? 1'b1 : 1'bz;  // Controlled_Buffer controlled_buffer_22
  assign Mem_str = T1 ? 1'b0 : 1'bz;  // Controlled_Buffer controlled_buffer_23
  assign Mem_sel = T1 ? 1'b0 : 1'bz;  // Controlled_Buffer controlled_buffer_24
  assign Mem_clr = T1 ? 1'b0 : 1'bz;  // Controlled_Buffer controlled_buffer_25
  assign AR_FunSel = T1 ? 2'b10 : 2'bz;  // Controlled_Buffer controlled_buffer_26
  assign AR_RegSel = T1 ? 3'b001 : 3'bz;  // Controlled_Buffer controlled_buffer_27
  assign AR_OutCSel = T1 ? 2'b10 : 2'bz;  // Controlled_Buffer controlled_buffer_28
  Decoder #(.select(5), .enable("false")) decoder_3 (
    .out0(D00), .out1(D01), .out2(D02), .out3(D03), .out4(D04), .out5(D05), .out6(D06), .out7(D07),
    .out8(D08), .out9(D09), .out10(D0A), .out11(D0B), .out12(D0C), .out13(D0D), .out14(D0E), .sel(Instruction));  // open: out15, out16, out17, out18, out19, out20, out21, out22, out23, out24, out25, out26, out27, out28, out29, out30, out31
  not not_4 (not_4_out, ADDRMODE);
  and and_13 (and_13_out, and_11_out, not_4_out);
  assign AR_FunSel = and_13_out ? 2'b00 : 2'bz;  // Controlled_Buffer controlled_buffer_29
  assign AR_RegSel = and_13_out ? 3'b100 : 3'bz;  // Controlled_Buffer controlled_buffer_30
  assign MuxBSel = and_13_out ? 2'b01 : 2'bz;  // Controlled_Buffer controlled_buffer_31
  not not_5 (not_5_out, ADDRMODE);
  and and_14 (and_14_out, and_12_out, not_5_out);
  assign SC_Reset = and_14_out ? 1'b1 : 1'bz;  // Controlled_Buffer controlled_buffer_32
  assign IR_Enable = T2 ? 1'b0 : 1'bz;  // Controlled_Buffer controlled_buffer_33
  not not_6 (not_6_out, ADDRMODE);
  and and_15 (and_15_out, D0A, T3);
  and and_16 (and_16_out, and_15_out, not_6_out);
  assign RF_OutASel = and_16_out ? DESTREG : 2'bz;  // Controlled_Buffer controlled_buffer_34
  assign ALU_FunSel = and_16_out ? 4'b0100 : 4'bz;  // Controlled_Buffer controlled_buffer_35
  assign AR_OutCSel = and_16_out ? 2'b00 : 2'bz;  // Controlled_Buffer controlled_buffer_36
  assign Mem_sel = and_16_out ? 1'b0 : 1'bz;  // Controlled_Buffer controlled_buffer_37
  assign Mem_str = and_16_out ? 1'b1 : 1'bz;  // Controlled_Buffer controlled_buffer_38
  assign Mem_load = and_16_out ? 1'b0 : 1'bz;  // Controlled_Buffer controlled_buffer_39
  and and_17 (and_17_out, D0B, T2);
  assign RF_RegSel = and_21_out ? decoder_4_out3 : 4'bz;  // Controlled_Buffer controlled_buffer_40
  assign AR_RegSel = and_21_out ? or_1_out : 3'bz;  // Controlled_Buffer controlled_buffer_41
  and and_18 (and_18_out, D0B, T3);
  and and_19 (and_19_out, and_18_out, and_22_out);
  assign SC_Reset = and_19_out ? 1'b1 : 1'bz;  // Controlled_Buffer controlled_buffer_42
  not not_7 (not_7_out, ADDRESS[7]);
  not not_8 (not_8_out, DESTREG[2]);
  and and_20 (and_20_out, not_8_out, not_7_out);
  and and_21 (and_21_out, and_17_out, and_20_out);
  assign RF_OutSel = and_21_out ? ADDRESS[6:5] : 2'bz;  // Controlled_Buffer controlled_buffer_43
  assign ALU_FunSel = and_21_out ? 4'b0100 : 4'bz;  // Controlled_Buffer controlled_buffer_44
  assign MuxASel = and_21_out ? 2'b11 : 2'bz;  // Controlled_Buffer controlled_buffer_45
  Decoder #(.select(3), .disabled(0)) decoder_4 (
    .out0(decoder_4_out3[3]), .out1(decoder_4_out3[2]), .out2(decoder_4_out3[1]), .out3(decoder_4_out3[0]),
    .out4(or_1_out[2]), .out5(or_1_out[1]), .out6(decoder_4_out6), .out7(decoder_4_out7),
    .sel({DESTREG, ADDRMODE}), .en(and_21_out));
  not not_9 (not_9_out, ADDRESS[7]);
  not not_10 (not_10_out, DESTREG[2]);
  and and_22 (and_22_out, not_10_out, not_9_out);
  or or_1 (or_1_out[0], decoder_4_out6, decoder_4_out7);
  and and_23 (and_23_out, D04, T2);
  and and_24 (and_24_out, and_23_out, ADDRMODE);
  assign MuxBSel = and_24_out ? 2'b01 : 2'bz;  // Controlled_Buffer controlled_buffer_46
  assign AR_RegSel = and_24_out ? 3'b001 : 3'bz;  // Controlled_Buffer controlled_buffer_47
  assign AR_FunSel = and_24_out ? 2'b00 : 2'bz;  // Controlled_Buffer controlled_buffer_48
  and and_25 (and_25_out, D04, T3);
  and and_26 (and_26_out, and_25_out, ADDRMODE);
  assign SC_Reset = and_26_out ? 1'b1 : 1'bz;  // Controlled_Buffer controlled_buffer_49
  and and_27 (and_27_out, D0B, T2);
  and and_28 (and_28_out, D0B, T3);
  and and_29 (and_29_out, and_27_out, xor_1_out);
  assign RF_OutSel = and_29_out ? ADDRESS[6:5] : 2'bz;  // Controlled_Buffer controlled_buffer_50
  assign ALU_FunSel = and_29_out ? 4'b0100 : 4'bz;  // Controlled_Buffer controlled_buffer_51
  assign MuxBSel = and_29_out ? 2'b11 : 2'bz;  // Controlled_Buffer controlled_buffer_52
  Decoder #(.select(3), .disabled(0)) decoder_5 (
    .out0(decoder_5_out3[3]), .out1(decoder_5_out3[2]), .out2(decoder_5_out3[1]), .out3(decoder_5_out3[0]),
    .out4(or_2_out[2]), .out5(or_2_out[1]), .out6(decoder_5_out6), .out7(decoder_5_out7),
    .sel({DESTREG, ADDRMODE}), .en(and_29_out));
  assign RF_RegSel = and_29_out ? decoder_5_out3 : 4'bz;  // Controlled_Buffer controlled_buffer_53
  assign AR_RegSel = and_29_out ? or_2_out : 3'bz;  // Controlled_Buffer controlled_buffer_54
  assign AR_OutCSel = and_29_out ? ADDRESS[6:5] : 2'bz;  // Controlled_Buffer controlled_buffer_55
  assign MuxASel = and_29_out ? 2'b10 : 2'bz;  // Controlled_Buffer controlled_buffer_56
  and and_30 (and_30_out, and_28_out, xor_2_out);
  assign SC_Reset = and_30_out ? 1'b1 : 1'bz;  // Controlled_Buffer controlled_buffer_57
  xor xor_1 (xor_1_out, DESTREG[2], ADDRESS[7]);
  or or_2 (or_2_out[0], decoder_5_out6, decoder_5_out7);
  xor xor_2 (xor_2_out, DESTREG[2], ADDRESS[7]);
  and and_31 (and_31_out, D05, D05, T2);
  and and_32 (and_32_out, D05, D05, T3);
  and and_33 (and_33_out, and_31_out, ADDRMODE);
  assign MuxBSel = and_33_out ? 2'b01 : 2'bz;  // Controlled_Buffer controlled_buffer_58
  assign AR_RegSel = and_33_out ? 3'b001 : 3'bz;  // Controlled_Buffer controlled_buffer_59
  assign AR_FunSel = and_33_out ? 2'b00 : 2'bz;  // Controlled_Buffer controlled_buffer_60
  and and_34 (and_34_out, and_32_out, ADDRMODE);
  assign SC_Reset = and_34_out ? 1'b1 : 1'bz;  // Controlled_Buffer controlled_buffer_61
  and and_35 (and_35_out, D0B, T2);
  and and_36 (and_36_out, D0B, T3);
  and and_37 (and_37_out, D0B, T4);
  and and_38 (and_38_out, and_37_out, and_43_out);
  and and_39 (and_39_out, DESTREG[2], ADDRESS[7]);
  and and_40 (and_40_out, and_35_out, and_39_out);
  assign AR_OutCSel = and_40_out ? ADDRESS[6:5] : 2'bz;  // Controlled_Buffer controlled_buffer_62
  assign MuxASel = and_40_out ? 2'b10 : 2'bz;  // Controlled_Buffer controlled_buffer_63
  assign RF_RegSel = and_40_out ? 4'b0001 : 4'bz;  // Controlled_Buffer controlled_buffer_64
  and and_41 (and_41_out, DESTREG[2], ADDRESS[7]);
  and and_42 (and_42_out, and_36_out, and_41_out);
  assign RF_OutASel = and_42_out ? 2'b11 : 2'bz;  // Controlled_Buffer controlled_buffer_65
  assign ALU_FunSel = and_42_out ? 4'b0100 : 4'bz;  // Controlled_Buffer controlled_buffer_66
  assign MuxBSel = and_42_out ? 2'b11 : 2'bz;  // Controlled_Buffer controlled_buffer_67
  Decoder #(.select(3), .disabled(0)) decoder_6 (
    .out4(or_3_out[2]), .out5(or_3_out[1]), .out6(decoder_6_out6), .out7(decoder_6_out7),
    .sel({DESTREG, ADDRMODE}), .en(and_42_out));  // open: out0, out1, out2, out3
  assign AR_RegSel = and_42_out ? or_3_out : 3'bz;  // Controlled_Buffer controlled_buffer_68
  and and_43 (and_43_out, DESTREG[2], ADDRESS[7]);
  assign SC_Reset = and_38_out ? 1'b1 : 1'bz;  // Controlled_Buffer controlled_buffer_69
  or or_3 (or_3_out[0], decoder_6_out6, decoder_6_out7);
  not not_11 (not_11_out, D05);
  not not_12 (not_12_out, D05);
  and and_44 (and_44_out, not_11_out, D06, T2);
  and and_45 (and_45_out, and_44_out, ADDRMODE);
  assign MuxBSel = and_45_out ? 2'b01 : 2'bz;  // Controlled_Buffer controlled_buffer_70
  assign AR_RegSel = and_45_out ? 3'b001 : 3'bz;  // Controlled_Buffer controlled_buffer_71
  assign AR_FunSel = and_45_out ? 2'b00 : 2'bz;  // Controlled_Buffer controlled_buffer_72
  and and_46 (and_46_out, not_12_out, D06, T2);
  and and_47 (and_47_out, and_46_out, ADDRMODE);
  assign SC_Reset = and_47_out ? 1'b1 : 1'bz;  // Controlled_Buffer controlled_buffer_73

  // Other names for the same wires on the sheet: Instruction[10:0] = {DESTREG, ADDRMODE, ADDRESS};
  //   SRCREG2[2:0] = ADDRESS[4:2]; SRCREG1[2:0] = ADDRESS[7:5]; DESTREG[0] = ADDRMODE; REGSEL[1:0] = DESTREG;
  //   OPCODE[4:0] = Instruction; Z = D05

  // Notes on the sheet:
  //   Sequence Counter
  //   ORGANIZATION
  //   D09 - LD
  //   FETCH & DECODE
  //   D0A - ST
  //   RF TO RF
  //   D04 - BRA
  //   RF TO AR or AR TO RF
  //   D0B - MOV
  //   D05 - BEQ
  //   AR TO AR
  //   D06 - BNE
endmodule

module Sequence_Counter (
  input  Reset,
  output T0,
  output T1,
  output T2,
  output T3,
  output T4,
  output T5,
  output T6,
  output T7
);

  wire clock_1_out;
  wire [2:0] counter_1_q;

  Clock clock_1 (.out(clock_1_out));
  Counter #(.width(3), .max('h7)) counter_1 (
    .count(1'b1), .Q(counter_1_q), .clk(clock_1_out), .clr(Reset));  // open: load, D, carry, preset, down
  Decoder #(.select(3), .enable("false")) decoder_1 (
    .out0(T0), .out1(T1), .out2(T2), .out3(T3), .out4(T4), .out5(T5), .out6(T6), .out7(T7), .sel(counter_1_q));
endmodule
